# Fritzing sketch Harmony_RF_Outlet (saved by Fritzing 0.9.0b)
breadboards: 1

parts:
  U1 = RF-LINK_TX [package=rf-link_tx]
  IR1 = TSOP312.., 314.. [package=THT]
  Part1 = Arduino Pro Mini v13

nets:
  N1: U1.DATA, Part1.D4
  GND: U1.GND, IR1.GND, Part1.GND
  N2: U1.+5V, Part1.D7
  N3: IR1.Vs, Part1.VCC
  N4: IR1.Data, Part1.D2
